# Fritzing sketch lora_receiver (saved by Fritzing 1.0.6)
breadboards: 1

parts:
  Part1 = Arduino Pro Mini (3.3V)
  M1 = Osoyoo SX1278-ra-02
  LCD1 = LCD screen
  LCM1602_IIC1 = LCM1602 IIC [part_number="LCM1602 IIC" chip_label="LCM1602 IIC" package="DIP (Dual Inline) [THT]"]

nets:
  GND: Part1.GND, M1.GND, LCM1602_IIC1.GND, LCM1602_IIC1.SDA
  VCC: Part1.VCC, M1.3.3V, LCM1602_IIC1.VCC
  N1: Part1.SCK, M1.SCK
  N2: Part1.MISO, M1.MISO
  N3: Part1.MOSI, M1.MOSI
  N4: Part1.D10, M1.NSS
  N5: Part1.D9, M1.RST
  N6: Part1.D2, M1.DIO0
  VSS: LCD1.VSS, LCM1602_IIC1.VSS
  VDD: LCD1.VDD, LCM1602_IIC1.VDD
  N7: LCD1.V0, LCM1602_IIC1.V0
  N8: LCD1.RS, LCM1602_IIC1.RS
  N9: LCD1.R/W, LCM1602_IIC1.RW
  N10: LCD1.E, LCM1602_IIC1.E
  N11: LCD1.DB0, LCM1602_IIC1.D0
  N12: LCD1.DB1, LCM1602_IIC1.D1
  N13: LCD1.DB2, LCM1602_IIC1.D2
  N14: LCD1.DB3, LCM1602_IIC1.D3
  N15: LCD1.DB4, LCM1602_IIC1.D4
  N16: LCD1.DB5, LCM1602_IIC1.D5
  N17: LCD1.DB6, LCM1602_IIC1.D6
  N18: LCD1.DB7, LCM1602_IIC1.D7
  N19: LCD1.LED+, LCM1602_IIC1.A
  N20: LCD1.LED-, LCM1602_IIC1.K
  N21: LCM1602_IIC1.LED_A, LCM1602_IIC1.LED_B

custom parts:
  Osoyoo SX1278-ra-02: Osoyoo Long Distance wireless transceiver Uart LoRa Module.
  LCM1602 IIC: I2C-Module to use a 1602 or 2004 LCD on with the wire.h libory Serial LCD Modul
