# Fritzing sketch lora_receiver_nodemcu (saved by Fritzing 1.0.6)
breadboards: 1

parts:
  M1 = Osoyoo SX1278-ra-02
  LCD1 = LCD screen
  LCM1602_IIC1 = LCM1602 IIC [part_number="LCM1602 IIC" chip_label="LCM1602 IIC" package="DIP (Dual Inline) [THT]"]
  Mod1 = Amica NodeMCU DEVKIT 1.0

nets:
  GND: M1.GND, LCM1602_IIC1.GND, Mod1.pin2
  3.3V: M1.3.3V, LCM1602_IIC1.VCC, Mod1.pin1
  N1: M1.RST, Mod1.pin_15
  N2: M1.DIO0, Mod1.pin_11
  N3: M1.SCK, Mod1.pin8
  N4: M1.MISO, Mod1.pin7
  N5: M1.MOSI, Mod1.pin6
  N6: M1.NSS, Mod1.pin5
  VDD: LCD1.VDD, LCM1602_IIC1.VDD
  N7: LCD1.RS, LCM1602_IIC1.RS
  N8: LCD1.R/W, LCM1602_IIC1.RW
  N9: LCD1.E, LCM1602_IIC1.E
  N10: LCD1.DB0, LCM1602_IIC1.D0
  N11: LCD1.DB1, LCM1602_IIC1.D1
  N12: LCD1.DB2, LCM1602_IIC1.D2
  N13: LCD1.DB3, LCM1602_IIC1.D3
  N14: LCD1.DB4, LCM1602_IIC1.D4
  N15: LCD1.DB5, LCM1602_IIC1.D5
  N16: LCD1.DB6, LCM1602_IIC1.D6
  N17: LCD1.DB7, LCM1602_IIC1.D7
  N18: LCD1.LED+, LCM1602_IIC1.A
  N19: LCD1.LED-, LCM1602_IIC1.K
  N20: LCM1602_IIC1.SDA, Mod1.pin_13
  N21: LCM1602_IIC1.SCL, Mod1.pin_14
  N22: LCM1602_IIC1.LED_A, LCM1602_IIC1.LED_B

custom parts:
  Osoyoo SX1278-ra-02: Osoyoo Long Distance wireless transceiver Uart LoRa Module.
  LCM1602 IIC: I2C-Module to use a 1602 or 2004 LCD on with the wire.h libory Serial LCD Modul
